# Fritzing sketch HPV-Version 2 (saved by Fritzing 0.9.3b)
breadboards: 1

parts:
  C1 = Capacitor [package=cap-pth-small]
  C3 = Capacitor Polarized [package=cpol-radial-10uf-25v]
  IC1 = Polar RE07S Heart Rate Monitor
  C2 = Capacitor [package=cap-pth-small]
  Part1 = Adafruit GPS FeatherWing [part_number="Adafruit #3133"]  # not connected
  Part4 = RFID-RC522-v2
  Part5 = Adafruit HUZZAH32 ESP32 Feather [part_number="Adafruit #3405"]
  SIM800L_BO1 = SIM800L BO
  R1 = Resistor [tolerance=±5% resistance=100k package=THT]
  R2 = Resistor [tolerance=±5% resistance=100k package=THT]
  U1 = mystery part, 3 pins [chip_label=Hall]
  R3 = Resistor [tolerance=±5% resistance=680 package=THT]
  microSD1 = MicroSD Card Module
  C4 = Capacitor Polarized [package=cpol-radial-10uf-25v]
  R6 = Resistor [tolerance=±5% resistance=4.7k package=THT]
  R7 = Resistor [tolerance=±5% resistance=4.7k package=THT]
  DHT1 = DHT22 Humidity and Temperature Sensor
  Tiny_RTC1 = Tiny RTC
  R8 = Resistor [tolerance=±5% resistance=100k package=THT]

nets:
  GND: C1.1, C3.-, IC1.GND, C2.1, Part4.GND, Part5.GND, SIM800L_BO1.GND, R1.Pin_1, U1.pin2, microSD1.GND, C4.-, DHT1.GND, Tiny_RTC1.GND
  VCC: C1.2, C3.+, IC1.VCC, C2.2, Part4.3.3V, Part5.3.3V, SIM800L_BO1.NET, SIM800L_BO1.VCC, U1.pin1, R3.Pin_1, microSD1.VCC, C4.+, R6.Pin_1, R7.Pin_1, DHT1.VDD, Tiny_RTC1.VCC, R8.Pin_1
  N1: IC1.Pulse, Part5.A2_I34
  N2: Part4.SDA, Part5.A5_IO4
  N3: Part4.SCK, Part5.SCK, microSD1.SCK
  N4: Part4.MOSI, Part5.MOSI, microSD1.MOSI
  N5: Part4.MISO, Part5.MISO, microSD1.MISO
  N6: Part4.IRQ, Part5.A4_IO36
  N7: Part4.RST, Part5.RESET, SIM800L_BO1.RST
  N8: Part5.IO21, Tiny_RTC1.DS
  N9: Part5.A3_I39, U1.pin3, R3.Pin_0
  N10: Part5.A1_DAC1, R1.Pin_0, R2.Pin_1
  N11: Part5.A0_DAC2, microSD1.CS
  N12: Part5.VBUS, R2.Pin_0
  N13: Part5.IO27_A10, SIM800L_BO1.RXD
  N14: Part5.IO33_A9, SIM800L_BO1.TXD
  N15: Part5.IO15_A8, SIM800L_BO1.RING
  N16: Part5.IO32_A7, SIM800L_BO1.DTR
  N17: Part5.IO14_A6, DHT1.DATA, R8.Pin_0
  N18: Part5.SCL, R6.Pin_0, Tiny_RTC1.SCL
  N19: Part5.SDA, R7.Pin_0, Tiny_RTC1.SDA

custom parts:
  Polar RE07S Heart Rate Monitor: The Polar heart rate receiver.
  Adafruit GPS FeatherWing: Give your Feather a sense of place, with an Ultimate GPS FeatherWing. In 2013 we designed the Ultimate GPS module to satisfy all your GPS desires - and now we have brought its power and versatility plus more to our Feather series with the Adafruit Ultimate GPS FeatherWing! This FeatherWing plugs right into your Feather board and gives it a precise, sensitive, and low power GPS module for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
  RFID-RC522-v2: A simple China made RFID-RC522 Reader; do check the pin labels, as this is a MFRC522 based clone.
  Tiny RTC: Tiny RTC I2C module DS1370Z RTC and AT24C32 EEPROM
