# Fritzing sketch HPV (saved by Fritzing 0.9.3b)
circuit board: 8.46667cm x 5.64444cm
breadboards: 1

parts:
  Part2 = Logic Level Converter
  C1 = Capacitor [package=cap-pth-small]
  C3 = Capacitor Polarized [package=cpol-radial-10uf-25v]
  C4 = Capacitor Polarized [package=cpol-radial-10uf-25v]
  Part3 = Arduino Uno (Rev3) - ICSP
  IC1 = Polar RE07S Heart Rate Monitor [package="DIP (Dual Inline) [THT]"]
  C2 = Capacitor [package=cap-pth-small]
  Part1 = Adafruit GPS FeatherWing [part_number="Adafruit #3133"]
  Part4 = RFID-RC522-v2

nets:
  GND: Part2.GND, C1.1, C3.-, C4.-, Part3.GND, IC1.GND, C2.1, Part1.GND, Part4.GND
  3V3: Part2.LV, C1.2, C3.+, Part3.3V3, Part1.3V, Part4.3.3V
  N1: Part2.RX_LV, Part1.RX
  N2: Part2.TX_LV, Part1.TX
  N3: Part2.TX_HV, Part3.D6_PWM
  N4: Part2.RX_HV, Part3.D7
  5V: Part2.HV, C4.+, Part3.5V, IC1.VCC, C2.2
  N5: Part3.D8, IC1.Pulse
  N6: Part3.D10_PWM/SS, Part4.SDA
  N7: Part3.D11_PWM/MOSI, Part4.MOSI
  N8: Part3.D12/MISO, Part4.MISO
  N9: Part3.D13/SCK, Part4.SCK
  N10: Part3.D5_PWM, Part4.RST

custom parts:
  Polar RE07S Heart Rate Monitor: The Polar heart rate receiver.
  Adafruit GPS FeatherWing: Give your Feather a sense of place, with an Ultimate GPS FeatherWing. In 2013 we designed the Ultimate GPS module to satisfy all your GPS desires - and now we have brought its power and versatility plus more to our Feather series with the Adafruit Ultimate GPS FeatherWing! This FeatherWing plugs right into your Feather board and gives it a precise, sensitive, and low power GPS module for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
  RFID-RC522-v2: A simple China made RFID-RC522 Reader; do check the pin labels, as this is a MFRC522 based clone.
